# Fritzing sketch Display (saved by Fritzing 0.8.7b)
circuit board: 14.63cm x 11.4263cm
breadboards: 1

parts:
  LedF5 = LED - 5mm [color="Red (633nm)" package="5 mm [THT]"]
  LedF4 = LED - 5mm [color="Red (633nm)" package="5 mm [THT]"]
  LedF3 = LED - 5mm [color="Red (633nm)" package="5 mm [THT]"]
  LedF2 = LED - 5mm [color="Red (633nm)" package="5 mm [THT]"]
  LedF1 = LED - 5mm [color="Red (633nm)" package="5 mm [THT]"]
  LedE2 = LED - 5mm [color="Red (633nm)" package="5 mm [THT]"]
  LedE5 = LED - 5mm [color="Red (633nm)" package="5 mm [THT]"]
  LedE1 = LED - 5mm [color="Red (633nm)" package="5 mm [THT]"]
  LedE3 = LED - 5mm [color="Red (633nm)" package="5 mm [THT]"]
  LedE4 = LED - 5mm [color="Red (633nm)" package="5 mm [THT]"]
  LedG4 = LED - 5mm [color="Red (633nm)" package="5 mm [THT]"]
  LedG1 = LED - 5mm [color="Red (633nm)" package="5 mm [THT]"]
  LedG5 = LED - 5mm [color="Red (633nm)" package="5 mm [THT]"]
  LedG3 = LED - 5mm [color="Red (633nm)" package="5 mm [THT]"]
  LedG2 = LED - 5mm [color="Red (633nm)" package="5 mm [THT]"]
  LedA1 = LED - 5mm [color="Red (633nm)" package="5 mm [THT]"]
  LedA2 = LED - 5mm [color="Red (633nm)" package="5 mm [THT]"]
  LedA5 = LED - 5mm [color="Red (633nm)" package="5 mm [THT]"]
  LedA4 = LED - 5mm [color="Red (633nm)" package="5 mm [THT]"]
  LedA3 = LED - 5mm [color="Red (633nm)" package="5 mm [THT]"]
  LedD5 = LED - 5mm [color="Red (633nm)" package="5 mm [THT]"]
  LedD4 = LED - 5mm [color="Red (633nm)" package="5 mm [THT]"]
  LedD1 = LED - 5mm [color="Red (633nm)" package="5 mm [THT]"]
  LedD2 = LED - 5mm [color="Red (633nm)" package="5 mm [THT]"]
  LedD3 = LED - 5mm [color="Red (633nm)" package="5 mm [THT]"]
  ledC = LED - 5mm [color="Red (633nm)" package="5 mm [THT]"]
  ledC_2 = LED - 5mm [color="Red (633nm)" package="5 mm [THT]"]
  ledC_3 = LED - 5mm [color="Red (633nm)" package="5 mm [THT]"]
  ledC_4 = LED - 5mm [color="Red (633nm)" package="5 mm [THT]"]
  ledC_5 = LED - 5mm [color="Red (633nm)" package="5 mm [THT]"]
  LedB3 = LED - 5mm [color="Red (633nm)" package="5 mm [THT]"]
  LedB2 = LED - 5mm [color="Red (633nm)" package="5 mm [THT]"]
  LedB5 = LED - 5mm [color="Red (633nm)" package="5 mm [THT]"]
  LedB1 = LED - 5mm [color="Red (633nm)" package="5 mm [THT]"]
  LedB4 = LED - 5mm [color="Red (633nm)" package="5 mm [THT]"]
  J1 = male pin header, 8 pins [form="♂ (male)"]

nets:
  N1: LedF5.cathode, LedF4.cathode, LedF3.cathode, LedF2.cathode, LedF1.cathode, J1.pin6
  N2: LedF5.anode, LedF4.anode, LedF3.anode, LedF2.anode, LedF1.anode, LedE2.anode, LedE5.anode, LedE1.anode, LedE3.anode, LedE4.anode, LedG4.anode, LedG1.anode, LedG5.anode, LedG3.anode, LedG2.anode, LedA1.anode, LedA2.anode, LedA5.anode, LedA4.anode, LedA3.anode, LedD5.anode, LedD4.anode, LedD1.anode, LedD2.anode, LedD3.anode, ledC.anode, ledC_2.anode, ledC_3.anode, ledC_4.anode, ledC_5.anode, LedB3.anode, LedB2.anode, LedB5.anode, LedB1.anode, LedB4.anode, J1.pin8
  N3: LedE2.cathode, LedE5.cathode, LedE1.cathode, LedE3.cathode, LedE4.cathode, J1.pin5
  N4: LedG4.cathode, LedG1.cathode, LedG5.cathode, LedG3.cathode, LedG2.cathode, J1.pin7
  N5: LedA1.cathode, LedA2.cathode, LedA5.cathode, LedA4.cathode, LedA3.cathode, J1.pin1
  N6: LedD5.cathode, LedD4.cathode, LedD1.cathode, LedD2.cathode, LedD3.cathode, J1.pin4
  N7: ledC.cathode, ledC_2.cathode, ledC_3.cathode, ledC_4.cathode, ledC_5.cathode, J1.pin3
  N8: LedB3.cathode, LedB2.cathode, LedB5.cathode, LedB1.cathode, LedB4.cathode, J1.pin2
